# Fritzing sketch Untitled Sketch 3 (saved by Fritzing 0.9.3b)
breadboards: 1

parts:
  Part1 = Arduino Uno (Rev3)
  e-radionica1 = TCS230 Color Sensor [part_number=101209]
  Part2 = LCD1602-I2C
  J1 = Basic Servo
  S3 = Pushbutton [package="[THT]"]
  S4 = Pushbutton [package="[THT]"]
  J2 = Basic Servo
  Bat1 = battery_holder_single_18650
  Bat2 = battery_holder_single_18650
  Bat3 = battery_holder_single_18650
  Bat4 = battery_holder_single_18650

nets:
  N1: Part1.A4/SDA, Part2.SDA
  N2: Part1.A5/SCL, Part2.SCL
  N3: Part1.D8, e-radionica1.S3
  N4: Part1.D9_PWM, e-radionica1.Out
  N5: Part1.D10_PWM/SS, J1.pulse
  N6: Part1.D11_PWM/MOSI, J2.pulse
  N7: Part1.D2, S3.Pin_3, S3.Pin_4
  N8: Part1.D3_PWM, S4.Pin_3, S4.Pin_4
  N9: Part1.D5_PWM, e-radionica1.S0
  N10: Part1.D6_PWM, e-radionica1.S1
  N11: Part1.D7, e-radionica1.S2
  VCC: Part1.5V, e-radionica1.Vcc, Part2.VCC
  GND: Part1.GND, e-radionica1.Gnd, e-radionica1.OE, Part2.GND, J1.gnd, S3.Pin_1, S3.Pin_2, S4.Pin_1, S4.Pin_2, J2.gnd, Bat1.+, Bat2.-, Bat3.+, Bat4.-
  N12: J1.vcc, Bat1.-, Bat2.+, Bat3.-, Bat4.+

custom parts:
  TCS230 Color Sensor: TCS230
  LCD1602-I2C: A standard character display, usually with 2x16 characters. Comes in many colors with LCM1602 IIC attached.
  battery_holder_single_18650: single 18650 battery holder
